// Logisim project architectural_state.circ as structural Verilog: 8 circuits, main circuit main
module main (
  input  in_1,
  input  [4:0] in_2
);

  wire alu_1_zero, and_1_out, clock_1_out, clock_2_out, control_unit_1_alusrc, control_unit_1_branch,
       control_unit_1_memtoreg, control_unit_1_memwrite, control_unit_1_regdst, control_unit_1_regwrite;
  wire [2:0] control_unit_1_aluop;
  wire [4:0] instruction_memory_data_3, multiplexer_2_out;
  wire [5:0] instruction_memory_data;
  wire [31:0] adder_1_out, adder_2_out, alu_1_y, bit_extender_1_out, data_memory_dout, multiplexer_1_out,
       multiplexer_3_out, multiplexer_4_out, PC_q, register_file_1_rd1, register_file_1_rd2, shifter_1_out;
  wire [31:6] instruction_memory_data_2;

  Multiplexer #(.width(32)) multiplexer_1 (
    .in0(adder_1_out), .in1(adder_2_out), .out(multiplexer_1_out), .sel(and_1_out));
  Register #(.width(32)) PC (.D(multiplexer_1_out), .en(1'b1), .clk(clock_1_out), .Q(PC_q));  // open: clr
  Clock clock_1 (.out(clock_1_out));
  Adder #(.width(32)) adder_1 (.a(PC_q), .b({32{1'b0}}), .out(adder_1_out), .cin(in_1));  // open: cout
  ROM #(.addrWidth(16), .dataWidth(32)) instruction_memory (
    .addr(PC_q[17:2]),
    .data({instruction_memory_data_2[31], instruction_memory_data_3, instruction_memory_data_2[25:6], instruction_memory_data}));
  Control_Unit control_unit_1 (
    .Opcode(instruction_memory_data), .funct(instruction_memory_data_3), .RegDst(control_unit_1_regdst),
    .ALUSrc(control_unit_1_alusrc), .MemToReg(control_unit_1_memtoreg), .RegWrite(control_unit_1_regwrite),
    .MemWrite(control_unit_1_memwrite), .Branch(control_unit_1_branch), .ALUOp(control_unit_1_aluop));
  Multiplexer #(.width(5)) multiplexer_2 (
    .in0(instruction_memory_data_2[20:16]), .in1(instruction_memory_data_2[15:11]), .out(multiplexer_2_out),
    .sel(control_unit_1_regdst));
  assign bit_extender_1_out = {{16{instruction_memory_data_2[15]}}, {instruction_memory_data_2[15:6], instruction_memory_data}};  // Bit_Extender bit_extender_1
  Shifter #(.width(32)) shifter_1 (.in(bit_extender_1_out), .\dist (in_2), .out(shifter_1_out));
  Adder #(.width(32)) adder_2 (.a(shifter_1_out), .b(adder_1_out), .out(adder_2_out));  // open: cin, cout
  Register_File register_file_1 (
    .WD3(multiplexer_4_out), .Address_2(instruction_memory_data_2[20:16]),
    .Address_1(instruction_memory_data_2[25:21]), .Address_3(multiplexer_2_out),
    .WriteEnable(control_unit_1_regwrite), .RD1(register_file_1_rd1), .RD2(register_file_1_rd2));
  Multiplexer #(.width(32)) multiplexer_3 (
    .in0(register_file_1_rd2), .in1(bit_extender_1_out), .out(multiplexer_3_out), .sel(control_unit_1_alusrc));
  and and_1 (and_1_out, control_unit_1_branch, alu_1_zero);
  ALU alu_1 (.A(register_file_1_rd1), .B(multiplexer_3_out), .F(control_unit_1_aluop), .Y(alu_1_y), .Zero(alu_1_zero));
  RAM #(.addrWidth(16), .asyncread("true"), .dataWidth(32)) data_memory (
    .addr(alu_1_y[17:2]), .we(control_unit_1_memwrite), .oe(1'b1), .clk(clock_2_out),
    .din(register_file_1_rd2), .dout(data_memory_dout));
  Clock clock_2 (.out(clock_2_out));
  Multiplexer #(.width(32)) multiplexer_4 (
    .in0(alu_1_y), .in1(data_memory_dout), .out(multiplexer_4_out), .sel(control_unit_1_memtoreg));

  // Notes on the sheet:
  //   in_2: initial=0x2
  //   contents of instruction_memory (hex, n*v repeats v):
  //   20100024 ac100004 8c110004 2231ffff 2114022 1114824 1109fff9
endmodule

module Register_File (
  input  [4:0] Address_2,
  input  [4:0] Address_1,
  input  [31:0] WD3,
  input  [4:0] Address_3,
  input  WriteEnable,
  output [31:0] RD1,
  output [31:0] RD2
);

  wire decoder_1_out0, decoder_1_out1, decoder_1_out2, decoder_1_out3, decoder_1_out4, decoder_1_out5,
       decoder_1_out6, decoder_1_out7, decoder_1_out8, decoder_1_out9, decoder_1_out10, decoder_1_out11,
       decoder_1_out12, decoder_1_out13, decoder_1_out14, decoder_1_out15, decoder_1_out16, decoder_1_out17,
       decoder_1_out18, decoder_1_out19, decoder_1_out20, decoder_1_out21, decoder_1_out22, decoder_1_out23,
       decoder_1_out24, decoder_1_out25, decoder_1_out26, decoder_1_out27, decoder_1_out28, decoder_1_out29,
       decoder_1_out30, decoder_1_out31, decoder_2_out0, decoder_2_out1, decoder_2_out2, decoder_2_out3,
       decoder_2_out4, decoder_2_out5, decoder_2_out6, decoder_2_out7, decoder_2_out8, decoder_2_out9,
       decoder_2_out10, decoder_2_out11, decoder_2_out12, decoder_2_out13, decoder_2_out14, decoder_2_out15,
       decoder_2_out16, decoder_2_out17, decoder_2_out18, decoder_2_out19, decoder_2_out20, decoder_2_out21,
       decoder_2_out22, decoder_2_out23, decoder_2_out24, decoder_2_out25, decoder_2_out26, decoder_2_out27,
       decoder_2_out28, decoder_2_out29, decoder_2_out30, decoder_2_out31, decoder_3_out1, decoder_3_out2,
       decoder_3_out3, decoder_3_out4, decoder_3_out5, decoder_3_out6, decoder_3_out7, decoder_3_out8,
       decoder_3_out9, decoder_3_out10, decoder_3_out11, decoder_3_out12, decoder_3_out13, decoder_3_out14,
       decoder_3_out15, decoder_3_out16, decoder_3_out17, decoder_3_out18, decoder_3_out19, decoder_3_out20,
       decoder_3_out21, decoder_3_out22, decoder_3_out23, decoder_3_out24, decoder_3_out25, decoder_3_out26,
       decoder_3_out27, decoder_3_out28, decoder_3_out29, decoder_3_out30, decoder_3_out31;

  Decoder #(.enable("false"), .select(5)) decoder_1 (
    .out0(decoder_1_out0), .out1(decoder_1_out1), .out2(decoder_1_out2), .out3(decoder_1_out3),
    .out4(decoder_1_out4), .out5(decoder_1_out5), .out6(decoder_1_out6), .out7(decoder_1_out7),
    .out8(decoder_1_out8), .out9(decoder_1_out9), .out10(decoder_1_out10), .out11(decoder_1_out11),
    .out12(decoder_1_out12), .out13(decoder_1_out13), .out14(decoder_1_out14), .out15(decoder_1_out15),
    .out16(decoder_1_out16), .out17(decoder_1_out17), .out18(decoder_1_out18), .out19(decoder_1_out19),
    .out20(decoder_1_out20), .out21(decoder_1_out21), .out22(decoder_1_out22), .out23(decoder_1_out23),
    .out24(decoder_1_out24), .out25(decoder_1_out25), .out26(decoder_1_out26), .out27(decoder_1_out27),
    .out28(decoder_1_out28), .out29(decoder_1_out29), .out30(decoder_1_out30), .out31(decoder_1_out31),
    .sel(Address_2));
  Decoder #(.enable("false"), .select(5)) decoder_2 (
    .out0(decoder_2_out0), .out1(decoder_2_out1), .out2(decoder_2_out2), .out3(decoder_2_out3),
    .out4(decoder_2_out4), .out5(decoder_2_out5), .out6(decoder_2_out6), .out7(decoder_2_out7),
    .out8(decoder_2_out8), .out9(decoder_2_out9), .out10(decoder_2_out10), .out11(decoder_2_out11),
    .out12(decoder_2_out12), .out13(decoder_2_out13), .out14(decoder_2_out14), .out15(decoder_2_out15),
    .out16(decoder_2_out16), .out17(decoder_2_out17), .out18(decoder_2_out18), .out19(decoder_2_out19),
    .out20(decoder_2_out20), .out21(decoder_2_out21), .out22(decoder_2_out22), .out23(decoder_2_out23),
    .out24(decoder_2_out24), .out25(decoder_2_out25), .out26(decoder_2_out26), .out27(decoder_2_out27),
    .out28(decoder_2_out28), .out29(decoder_2_out29), .out30(decoder_2_out30), .out31(decoder_2_out31),
    .sel(Address_1));
  Decoder #(.select(5)) decoder_3 (
    .out1(decoder_3_out1), .out2(decoder_3_out2), .out3(decoder_3_out3), .out4(decoder_3_out4),
    .out5(decoder_3_out5), .out6(decoder_3_out6), .out7(decoder_3_out7), .out8(decoder_3_out8),
    .out9(decoder_3_out9), .out10(decoder_3_out10), .out11(decoder_3_out11), .out12(decoder_3_out12),
    .out13(decoder_3_out13), .out14(decoder_3_out14), .out15(decoder_3_out15), .out16(decoder_3_out16),
    .out17(decoder_3_out17), .out18(decoder_3_out18), .out19(decoder_3_out19), .out20(decoder_3_out20),
    .out21(decoder_3_out21), .out22(decoder_3_out22), .out23(decoder_3_out23), .out24(decoder_3_out24),
    .out25(decoder_3_out25), .out26(decoder_3_out26), .out27(decoder_3_out27), .out28(decoder_3_out28),
    .out29(decoder_3_out29), .out30(decoder_3_out30), .out31(decoder_3_out31), .sel(Address_3),
    .en(WriteEnable));  // open: out0
  Reg_Zero ZERO (.in_1(decoder_2_out0), .in_2(decoder_1_out0), .DATA_A_8cabddb7(RD1), .DATA_B_19affd4d(RD2));
  Reg_32 AT (
    .WriteData(WD3), .WriteEn(decoder_3_out1), .DataA(decoder_2_out1), .DataB(decoder_1_out1), .OutputA(RD1),
    .OutputB(RD2));
  Reg_32 V0 (
    .WriteData(WD3), .WriteEn(decoder_3_out2), .DataA(decoder_2_out2), .DataB(decoder_1_out2), .OutputA(RD1),
    .OutputB(RD2));
  Reg_32 V1 (
    .WriteData(WD3), .WriteEn(decoder_3_out3), .DataA(decoder_2_out3), .DataB(decoder_1_out3), .OutputA(RD1),
    .OutputB(RD2));
  Reg_32 A0 (
    .WriteData(WD3), .WriteEn(decoder_3_out4), .DataA(decoder_2_out4), .DataB(decoder_1_out4), .OutputA(RD1),
    .OutputB(RD2));
  Reg_32 A1 (
    .WriteData(WD3), .WriteEn(decoder_3_out5), .DataA(decoder_2_out5), .DataB(decoder_1_out5), .OutputA(RD1),
    .OutputB(RD2));
  Reg_32 A2 (
    .WriteData(WD3), .WriteEn(decoder_3_out6), .DataA(decoder_2_out6), .DataB(decoder_1_out6), .OutputA(RD1),
    .OutputB(RD2));
  Reg_32 A3 (
    .WriteData(WD3), .WriteEn(decoder_3_out7), .DataA(decoder_2_out7), .DataB(decoder_1_out7), .OutputA(RD1),
    .OutputB(RD2));
  Reg_32 T0 (
    .WriteData(WD3), .WriteEn(decoder_3_out8), .DataA(decoder_2_out8), .DataB(decoder_1_out8), .OutputA(RD1),
    .OutputB(RD2));
  Reg_32 T1 (
    .WriteData(WD3), .WriteEn(decoder_3_out9), .DataA(decoder_2_out9), .DataB(decoder_1_out9), .OutputA(RD1),
    .OutputB(RD2));
  Reg_32 T2 (
    .WriteData(WD3), .WriteEn(decoder_3_out10), .DataA(decoder_2_out10), .DataB(decoder_1_out10),
    .OutputA(RD1), .OutputB(RD2));
  Reg_32 T3 (
    .WriteData(WD3), .WriteEn(decoder_3_out11), .DataA(decoder_2_out11), .DataB(decoder_1_out11),
    .OutputA(RD1), .OutputB(RD2));
  Reg_32 T4 (
    .WriteData(WD3), .WriteEn(decoder_3_out12), .DataA(decoder_2_out12), .DataB(decoder_1_out12),
    .OutputA(RD1), .OutputB(RD2));
  Reg_32 T5 (
    .WriteData(WD3), .WriteEn(decoder_3_out13), .DataA(decoder_2_out13), .DataB(decoder_1_out13),
    .OutputA(RD1), .OutputB(RD2));
  Reg_32 T6 (
    .WriteData(WD3), .WriteEn(decoder_3_out14), .DataA(decoder_2_out14), .DataB(decoder_1_out14),
    .OutputA(RD1), .OutputB(RD2));
  Reg_32 T7 (
    .WriteData(WD3), .WriteEn(decoder_3_out15), .DataA(decoder_2_out15), .DataB(decoder_1_out15),
    .OutputA(RD1), .OutputB(RD2));
  Reg_32 S0 (
    .WriteData(WD3), .WriteEn(decoder_3_out16), .DataA(decoder_2_out16), .DataB(decoder_1_out16),
    .OutputA(RD1), .OutputB(RD2));
  Reg_32 S1 (
    .WriteData(WD3), .WriteEn(decoder_3_out17), .DataA(decoder_2_out17), .DataB(decoder_1_out17),
    .OutputA(RD1), .OutputB(RD2));
  Reg_32 S2 (
    .WriteData(WD3), .WriteEn(decoder_3_out18), .DataA(decoder_2_out18), .DataB(decoder_1_out18),
    .OutputA(RD1), .OutputB(RD2));
  Reg_32 S3 (
    .WriteData(WD3), .WriteEn(decoder_3_out19), .DataA(decoder_2_out19), .DataB(decoder_1_out19),
    .OutputA(RD1), .OutputB(RD2));
  Reg_32 S4 (
    .WriteData(WD3), .WriteEn(decoder_3_out20), .DataA(decoder_2_out20), .DataB(decoder_1_out20),
    .OutputA(RD1), .OutputB(RD2));
  Reg_32 S5 (
    .WriteData(WD3), .WriteEn(decoder_3_out21), .DataA(decoder_2_out21), .DataB(decoder_1_out21),
    .OutputA(RD1), .OutputB(RD2));
  Reg_32 S6 (
    .WriteData(WD3), .WriteEn(decoder_3_out22), .DataA(decoder_2_out22), .DataB(decoder_1_out22),
    .OutputA(RD1), .OutputB(RD2));
  Reg_32 S7 (
    .WriteData(WD3), .WriteEn(decoder_3_out23), .DataA(decoder_2_out23), .DataB(decoder_1_out23),
    .OutputA(RD1), .OutputB(RD2));
  Reg_32 T8 (
    .WriteData(WD3), .WriteEn(decoder_3_out24), .DataA(decoder_2_out24), .DataB(decoder_1_out24),
    .OutputA(RD1), .OutputB(RD2));
  Reg_32 T9 (
    .WriteData(WD3), .WriteEn(decoder_3_out25), .DataA(decoder_2_out25), .DataB(decoder_1_out25),
    .OutputA(RD1), .OutputB(RD2));
  Reg_32 K0 (
    .WriteData(WD3), .WriteEn(decoder_3_out26), .DataA(decoder_2_out26), .DataB(decoder_1_out26),
    .OutputA(RD1), .OutputB(RD2));
  Reg_32 K1 (
    .WriteData(WD3), .WriteEn(decoder_3_out27), .DataA(decoder_2_out27), .DataB(decoder_1_out27),
    .OutputA(RD1), .OutputB(RD2));
  Reg_32 GP (
    .WriteData(WD3), .WriteEn(decoder_3_out28), .DataA(decoder_2_out28), .DataB(decoder_1_out28),
    .OutputA(RD1), .OutputB(RD2));
  Reg_32 SP (
    .WriteData(WD3), .WriteEn(decoder_3_out29), .DataA(decoder_2_out29), .DataB(decoder_1_out29),
    .OutputA(RD1), .OutputB(RD2));
  Reg_32 FP (
    .WriteData(WD3), .WriteEn(decoder_3_out30), .DataA(decoder_2_out30), .DataB(decoder_1_out30),
    .OutputA(RD1), .OutputB(RD2));
  Reg_32 RA (
    .WriteData(WD3), .WriteEn(decoder_3_out31), .DataA(decoder_2_out31), .DataB(decoder_1_out31),
    .OutputA(RD1), .OutputB(RD2));
  Pull_Resistor pull_resistor_1 (.node(RD1));
  Pull_Resistor pull_resistor_2 (.node(RD2));
endmodule

module Reg_32 (
  input  [31:0] WriteData,
  input  WriteEn,
  input  DataA,
  input  DataB,
  output [31:0] OutputA,
  output [31:0] OutputB
);

  wire clock_1_out;
  wire [31:0] register_1_q;

  Register #(.width(32)) register_1 (.D(WriteData), .en(WriteEn), .clk(clock_1_out), .Q(register_1_q));  // open: clr
  Clock clock_1 (.out(clock_1_out));
  assign OutputA = DataA ? register_1_q : 32'bz;  // Controlled_Buffer controlled_buffer_1
  assign OutputB = DataB ? register_1_q : 32'bz;  // Controlled_Buffer controlled_buffer_2
endmodule

module Reg_Zero (
  input  in_1,
  input  in_2,
  output [31:0] DATA_A_8cabddb7,
  output [31:0] DATA_B_19affd4d
);

  assign DATA_A_8cabddb7 = in_1 ? {32{1'b0}} : 32'bz;  // Controlled_Buffer controlled_buffer_1
  assign DATA_B_19affd4d = in_2 ? {32{1'b0}} : 32'bz;  // Controlled_Buffer controlled_buffer_2
endmodule

module ALU (
  input  [31:0] A,
  input  [31:0] B,
  input  [2:0] F,
  output [31:0] Y,
  output Zero
);

  wire [31:0] adder_1_out, and_1_out, bit_extender_1_out, multiplexer_2_out, not_1_out, or_1_out;

  Adder #(.width(32)) adder_1 (.a(multiplexer_2_out), .b(A), .out(adder_1_out), .cin(F[2]));  // open: cout
  Multiplexer #(.select(2), .width(32)) multiplexer_1 (
    .in0(and_1_out), .in1(or_1_out), .in2(adder_1_out), .in3(bit_extender_1_out), .out(Y), .sel(F[1:0]));
  assign not_1_out = ~B;  // NOT_Gate not_1, 32 bits wide
  Multiplexer #(.width(32)) multiplexer_2 (.in0(B), .in1(not_1_out), .out(multiplexer_2_out), .sel(F[2]));
  assign or_1_out = A | multiplexer_2_out;  // OR_Gate or_1, 32 bits wide
  assign and_1_out = A & multiplexer_2_out;  // AND_Gate and_1, 32 bits wide
  assign bit_extender_1_out = {{31{1'b0}}, adder_1_out[31]};  // Bit_Extender bit_extender_1
  and and_2 (Zero, ~Y[0], ~Y[1], ~Y[2], ~Y[3], ~Y[4], ~Y[5], ~Y[6], ~Y[7], ~Y[8], ~Y[9], ~Y[10], ~Y[11], ~Y[12], ~Y[13], ~Y[14], ~Y[15], ~Y[16], ~Y[17], ~Y[18], ~Y[19], ~Y[20], ~Y[21], ~Y[22], ~Y[23], ~Y[24], ~Y[25], ~Y[26], ~Y[27], ~Y[28], ~Y[29], ~Y[30], ~Y[31]);  // AND_Gate
endmodule

module ALU_Decoder (
  input  [1:0] ALUOp,
  input  [4:0] funct,
  output [2:0] ALUControl
);

  wire and_1_out, or_1_out;

  and and_1 (and_1_out, ALUOp[1], funct[1]);
  or or_1 (or_1_out, funct[0], funct[3]);
  or or_2 (ALUControl[2], ALUOp[0], and_1_out);
  and and_2 (ALUControl[0], ALUOp[1], or_1_out);
  or or_3 (ALUControl[1], ALUOp[1], funct[2]);
endmodule

module Main_Decoder (
  input  [5:0] Opcode,
  output RegDst,
  output ALUSrc,
  output MemToReg,
  output RegWrite,
  output MemWrite,
  output Branch,
  output [1:0] ALUOp
);

  wire addi_out, not_1_out, not_2_out, not_3_out, not_4_out, not_5_out, not_6_out, not_7_out, not_8_out,
       not_9_out, not_10_out, not_11_out, not_12_out, not_13_out, not_14_out, not_15_out, not_16_out,
       not_17_out, not_18_out, not_19_out, not_20_out, not_21_out;

  not not_1 (not_1_out, Opcode[0]);
  not not_2 (not_2_out, Opcode[1]);
  not not_3 (not_3_out, Opcode[2]);
  and R_Format (ALUOp[1], not_1_out, not_2_out, not_3_out, not_4_out, not_5_out, not_6_out);
  not not_4 (not_4_out, Opcode[3]);
  not not_5 (not_5_out, Opcode[4]);
  not not_6 (not_6_out, Opcode[5]);
  not not_7 (not_7_out, Opcode[2]);
  and lw (MemToReg, Opcode[0], Opcode[1], not_7_out, not_8_out, not_9_out, Opcode[5]);
  not not_8 (not_8_out, Opcode[3]);
  not not_9 (not_9_out, Opcode[4]);
  not not_10 (not_10_out, Opcode[2]);
  and sw (MemWrite, Opcode[0], Opcode[1], not_10_out, Opcode[3], not_11_out, Opcode[5]);
  not not_11 (not_11_out, Opcode[4]);
  not not_12 (not_12_out, Opcode[0]);
  not not_13 (not_13_out, Opcode[1]);
  and beq (ALUOp[0], not_12_out, not_13_out, Opcode[2], not_14_out, not_15_out, not_16_out);
  not not_14 (not_14_out, Opcode[3]);
  not not_15 (not_15_out, Opcode[4]);
  not not_16 (not_16_out, Opcode[5]);
  not not_17 (not_17_out, Opcode[0]);
  not not_18 (not_18_out, Opcode[1]);
  and addi (addi_out, not_17_out, not_18_out, Opcode[2], not_19_out, not_20_out, not_21_out);
  not not_19 (not_19_out, Opcode[3]);
  not not_20 (not_20_out, Opcode[4]);
  not not_21 (not_21_out, Opcode[5]);
  or or_1 (ALUSrc, MemWrite, addi_out, MemToReg);
  or or_2 (RegWrite, ALUOp[1], addi_out, MemToReg);

  assign Branch = ALUOp[0];
  assign RegDst = ALUOp[1];
endmodule

module Control_Unit (
  input  [5:0] Opcode,
  input  [4:0] funct,
  output RegDst,
  output ALUSrc,
  output MemToReg,
  output RegWrite,
  output MemWrite,
  output Branch,
  output [2:0] ALUOp
);

  wire [1:0] main_decoder_1_aluop;

  Main_Decoder main_decoder_1 (
    .Opcode(Opcode), .RegDst(RegDst), .ALUSrc(ALUSrc), .MemToReg(MemToReg), .RegWrite(RegWrite),
    .MemWrite(MemWrite), .Branch(Branch), .ALUOp(main_decoder_1_aluop));
  ALU_Decoder alu_decoder_1 (.ALUOp(main_decoder_1_aluop), .funct(funct), .ALUControl(ALUOp));
endmodule
